# Fritzing sketch protoload_fritzing (saved by Fritzing 0.8.7b)
breadboards: 2

parts:
  Part1 = Arduino Uno (Rev3)
  J1 = LOAD_CELL [package=1x03]
  IC1 = IC, DIP package, 8 pins [chip_label=IC]
  IC2 = IC, DIP package, 8 pins [chip_label=IC]
  IC3 = IC, DIP package, 8 pins [chip_label=IC]
  J2 = LOAD_CELL [package=1x03]
  R1 = Resistor [package="2512 [SMD]"]
  R2 = Resistor [package="2512 [SMD]"]
  R3 = Resistor [package="2512 [SMD]"]
  R4 = Resistor [package="2512 [SMD]"]
  R5 = Resistor [package="2512 [SMD]"]
  R6 = Resistor [package="2512 [SMD]"]
  R7 = Resistor [package="2512 [SMD]"]
  R8 = Resistor [package="2512 [SMD]"]
  C1 = Capacitor [package=cap-pth-small2]
  LCD1 = LCD screen

nets:
  N1: Part1.A0, R7.Pin_0, C1.2
  N2: Part1.A1, IC3.pin6, R7.Pin_1, R8.Pin_1
  N3: Part1.GND, J1.W, IC1.pin4, IC2.pin4, IC3.pin4, R1.Pin_1, C1.1
  N4: Part1.D2, LCD1.RS
  N5: Part1.D3_PWM, LCD1.E
  N6: Part1.D4, LCD1.DB4
  N7: Part1.D5_PWM, LCD1.DB5
  N8: Part1.D6_PWM, LCD1.DB6
  N9: Part1.D7, LCD1.DB7
  N10: Part1.5V, IC1.pin7, IC2.pin7, IC3.pin7, J2.W
  N11: J1.B, IC1.pin3, J2.B
  N12: J1.R, IC2.pin3, J2.R
  N13: IC1.pin2, R2.Pin_1, R3.Pin_0
  N14: IC1.pin6, R3.Pin_1, R5.Pin_1
  N15: IC2.pin2, R2.Pin_0, R4.Pin_1
  N16: IC2.pin6, R4.Pin_0, R6.Pin_1
  N17: IC3.pin2, R5.Pin_0, R8.Pin_0
  N18: IC3.pin3, R1.Pin_0, R6.Pin_0

notes:
  The load cell
  - Full bridge load cell arrangement.
  3 stage amplification, for low noise and high gain.
  can be replaced by INA125
  This 3 stage amp is basic behind instrumental amplifiers.
  Arduino UNO Rev 3
  16x2 LCD to display weight.
  - Components
  - - Arduino
  - - LCD
  - - Load cell arrangement
  - - 3 LM741 or 1 INA125 op amps
  - - resistor .
  - - a capacitor.
  - - wires to connect
  - Taking power from arduino board, and giving it to load cell arrangement.
  - Reading the sense from the load cell.
  - But needs an amplification step to make arduino can read values on analog.
  - To power arduino, 9-12 v adapter with 600 - 800mA will be fine.
  - This arrangement is lose and for test purpose.
  - Noise may there in reading which can be 1g to 10g +/-.
